# Fritzing sketch HelloWorld (saved by Fritzing 0.9.3b)
breadboards: 1

parts:
  Part1 = Adafruit Feather M0 Express [part_number="Adafruit #3403"]
  Part2 = Adafruit MPR121
  J1 = female pin header, 12 pins [form="♀ (female)"]
  J2 = Generic female header - 8 pins [form="♀ (female)" package=THT]
  Part3 = Lithium Ion Polymer Battery 3.7v 100mAh [part_number=1570]  # not connected

nets:
  GND: Part1.GND, Part2.GND, Part2.ADDR, J2.GND
  N1: Part1.MOSI, J2.Din
  N2: Part1.SCK, J2.CLK
  3.3V: Part1.+3V3, Part2.VIN, J2.Vcc
  N3: Part1.D11, J2.D_C
  N4: Part1.D10, J2.CS
  N5: Part1.D6, J2.RST
  N6: Part1.D5, J2.LED
  N7: Part1.SCL, Part2.SCL
  N8: Part1.SDA, Part2.SDA
  N9: Part2.ELEC11, J1.pin12
  N10: Part2.ELEC10, J1.pin11
  N11: Part2.ELEC9, J1.pin10
  N12: Part2.ELEC8, J1.pin9
  N13: Part2.ELEC7, J1.pin8
  N14: Part2.ELEC6, J1.pin7
  N15: Part2.ELEC5, J1.pin6
  N16: Part2.ELEC4, J1.pin5
  N17: Part2.ELEC3, J1.pin4
  N18: Part2.ELEC2, J1.pin3
  N19: Part2.ELEC1, J1.pin2
  N20: Part2.ELEC0, J1.pin1

notes:
  The pin socket next to the MPR121 is really loops of bare wire that I soldered leads from the foil areas covering countries or regions. I also covered the these "terminals" with heat shrink tubing.
  This pin array is actually one end of a ribbon cable. The other end is soldered to the Nokia 5110/3310 Monochrome LCD

custom parts:
  Adafruit Feather M0 Express: We love all our Feathers equally, but this Feather is very special. It's our first Feather that is specifically designed for use with CircuitPython! CircuitPython is our beginner-oriented flavor of MicroPython - and as the name hints at, its a small but full-featured version of the popular Python programming language specifically for use with circuitry and electronics. That doesn't mean you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
  Adafruit MPR121: Add lots of touch sensors to your next microcontroller project with this easy-to-use 12-channel capacitive touch sensor breakout board, starring the MPR121. This chip can handle up to 12 individual touch pads. The MPR121 has support for only I2C, which can be implemented with nearly any microcontroller. You can select one of 4 addresses with the ADDR pin, for a total of 48 capacitive touch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
  Generic female header - 8 pins: Generic female header
  Lithium Ion Polymer Battery 3.7v 100mAh: Lithium ion polymer (also known as 'lipo' or 'lipoly') batteries are thin, light and powerful. The output ranges from 4.2V when completely charged to 3.7V. This battery has a capacity of ~100mAh for a total of about 0.4 Wh. The batteries come pre-attached with a genuine 2-pin JST-PH connector as shown and include the necessary protection circuitry.
