# Fritzing sketch TeensyDisplayBoard (saved by Fritzing 0.9.5d)
breadboards: 1

parts:
  Part1 = OLED Monochrome 128x32 I2C [part_number=931]
  S1 = Momentary Switch [package=ksa_sealed_tac_switch]
  S2 = Momentary Switch [package=ksa_sealed_tac_switch]
  S3 = Momentary Switch [package=ksa_sealed_tac_switch]
  J2 = Generic shrouded header - 10 pins -- Corrected Pin Numbering [form="♂ (shrouded male)" package=THT]

nets:
  5V: Part1.VIN, J2.pin1
  GND: Part1.GND, S1.2, S1.4, S2.4, S3.2, S3.4, J2.pin2
  SCL: Part1.SCL, J2.pin8
  SDA: Part1.SDA, J2.pin9
  N1: S1.1, S1.3, J2.pin7
  N2: S2.1, J2.pin6
  N3: S3.1, S3.3, J2.pin5
  3.3V: J2.pin3

custom parts:
  OLED Monochrome 128x32 I2C: These displays are small, only about 1" diagonal, but very readable due to the high contrast of an OLED display. This display is made of 128x32 individual white OLED pixels, each one is turned on or off by the controller chip. Because the display makes its own light, no backlight is required. This reduces the power required to run the OLED and is why the display has such high contrast; we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
  Generic shrouded header - 10 pins -- Corrected Pin Numbering: Generic shrouded header
