# Fritzing sketch OnlyHerHairdresser (saved by Fritzing 0.9.3b)
breadboards: 1
stripboards: 2

parts:
  LED1 = RGB LED - (4 legs) [package="5 mm [THT]"]
  LED2 = RGB LED - (4 legs) [package="5 mm [THT]"]
  LED3 = RGB LED - (4 legs) [package="5 mm [THT]"]
  LED4 = RGB LED - (4 legs) [package="5 mm [THT]"]
  A1 = Quad NPN Driver transistor [part_number=MPQ3903 package="DIP (Dual Inline) [THT]"]
  R1 = Resistor [tolerance=±5% resistance=47 package=THT]
  R2 = Resistor [tolerance=±5% resistance=47 package=THT]
  R3 = Resistor [tolerance=±5% resistance=47 package=THT]
  R4 = Resistor [tolerance=±5% resistance=1k package=THT]
  R5 = Resistor [tolerance=±5% resistance=1k package=THT]
  R6 = Resistor [tolerance=±5% resistance=1k package=THT]
  S1 = Pushbutton [package="[THT]"]
  Part2 = Adafruit TCS34725 RGB Color Sensor [part_number="Adafruit #1334"]
  Part3 = Adafruit Feather M0 Express [part_number="Adafruit #3403"]
  J2 = male pin header, 2 pins [form="♂ (male)"]
  J3 = female pin header, 2 pins [form="♀ (female)"]
  J4 = female pin header, 7 pins [form="♀ (female)"]
  J5 = male pin header, 7 pins [form="♂ (male)"]
  J6 = female pin header, 4 pins [form="♀ (female)"]
  J7 = male pin header, 4 pins [form="♂ (male)"]

nets (from the schematic view):
  N1: LED1.red_cathode, LED2.red_cathode, LED3.red_cathode, LED4.red_cathode, J6.pin1
  N2: LED1.common_anode, LED2.common_anode, LED3.common_anode, LED4.common_anode, J6.pin4
  N3: LED1.green_cathode, LED2.green_cathode, LED3.green_cathode, LED4.green_cathode, J6.pin2
  N4: LED1.blue_cathode, LED2.blue_cathode, LED3.blue_cathode, LED4.blue_cathode, J6.pin3
  N5: A1.pin_1, R1.Pin_1
  N6: A1.pin_2, R4.Pin_0
  GND: A1.pin_3, A1.pin_5, A1.pin_10, Part3.GND, J2.pin1, J5.pin6
  N7: A1.pin_6, R5.Pin_0
  N8: A1.pin_7, R2.Pin_1
  N9: A1.pin_8, R3.Pin_1
  N10: A1.pin_9, R6.Pin_0
  N11: R1.Pin_0, J7.pin1
  N12: R2.Pin_0, J7.pin2
  N13: R3.Pin_0, J7.pin3
  N14: R4.Pin_1, Part3.D10
  N15: R5.Pin_1, Part3.D6
  N16: R6.Pin_1, Part3.D5
  N17: S1.Pin_1, S1.Pin_2, J3.pin1
  N18: S1.Pin_3, S1.Pin_4, J3.pin2
  N19: Part2.VIN, J4.pin7
  N20: Part2.GND, J4.pin6
  N21: Part2.+3V3, J4.pin5
  N22: Part2.SCL, J4.pin4
  N23: Part2.SDA, J4.pin3
  N24: Part2.INT, J4.pin2
  N25: Part2.LED_EN, J4.pin1
  3.3V: Part3.+3V3, J5.pin7
  Comm: Part3.VBAT, J7.pin4
  N26: Part3.D11, J2.pin2
  N27: Part3.SCL, J5.pin4
  N28: Part3.SDA, J5.pin3
  N29: J5.pin1, J5.pin2

custom parts:
  Adafruit TCS34725 RGB Color Sensor: Your electronics can now see in dazzling color with this lovely color light sensor. We found the best color sensor on the market, the TCS34725, which has RGB and Clear light sensing elements. An IR blocking filter, integrated on-chip and localized to the color sensing photodiodes, minimizes the IR spectral component of the incoming light and allows color measurements to be made accurately. The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
  Adafruit Feather M0 Express: We love all our Feathers equally, but this Feather is very special. It's our first Feather that is specifically designed for use with CircuitPython! CircuitPython is our beginner-oriented flavor of MicroPython - and as the name hints at, its a small but full-featured version of the popular Python programming language specifically for use with circuitry and electronics. That doesn't mean you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
