# Fritzing sketch PagingDrHowardEtAl (saved by Fritzing 0.9.3b)

parts:
  Part1 = Arduino Uno (Rev3)  # not connected
  Part2 = Adafruit Proto Shield R3 [part_number="Adafruit #2077"]
  J1 = female pin header, 3 pins [form="♀ (female)"]
  J2 = female pin header, 4 pins [form="♀ (female)"]
  J3 = female pin header, 5 pins [form="♀ (female)"]
  Part3 = Seven-Segment LED Backpack 1.2 Inch Digits [part_number=1269]
  Part4 = Bi-Color 24-Bar Bargraph w I2C Backpack [part_number=1721]

nets:
  GND: Part2.GND, Part2.N$115, Part2.P$5#161, Part2.P$6#162, Part2.1#205, Part2.P$5#206, J1.pin3, J2.pin2, J3.pin3, Part3.GND, Part4.GND
  N1: Part2.3.3V, Part2.1#129, Part2.P$5#130, Part2.P$6#131, Part2.AREF, J1.pin1
  N2: Part2.A0, Part2.1#132, Part2.P$5#133, J1.pin2
  N3: Part2.A4, Part2.1#166, Part2.P$5#167, Part2.P$6#168, J2.pin3, J3.pin4, Part3.SDA, Part4.SDA
  N4: Part2.A5, Part2.1#169, Part2.P$5#170, Part2.P$6#171, J2.pin4, J3.pin5, Part3.SCL, Part4.SCL
  VDD: Part2.1#172, Part2.P$5#173, Part2.P$6#174, Part2.1#193, Part2.P$5#194, Part2.+5V, J2.pin1, J3.pin1, J3.pin2, Part3.VDD, Part3.VCCIO, Part4.VDD

notes:
  I did not actually use a proto shield. Instead I used a (scrap) piece of stripboard (I buy the BPS 6U stripboards from Mouser and cut them up for random small projects). I also did not use headers either (except for pin headers between the stripboard scrap and the Uno). I soldered ribbon cables for the LED display units and cut the connector pins off the pulse sensor and soldered the wires to the stripboard. The three pin "header" is for the pulse sensor.

custom parts:
  Adafruit Proto Shield R3: This prototyping shield is the best out there (well, we think so, at least), and now is even better with Version R3 - updated for the most compatibility with just about all the Arduinos! It works with UNO, Mega, Leonardo, NG, Diecimila, Duemilanove, and compatible Arduinos. Yun's and Arduino Ethernets have a chunky Ethernet jack that gets in the way of stacking, you can use the stacking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
  Seven-Segment LED Backpack 1.2 Inch Digits: This jumbo 1.2" 7-segment LED display includes a driver chip for simple control via an I2C interface. The backpack features address-selection jumpers so you can connect up to eight displays on a single I2C bus.
  Bi-Color 24-Bar Bargraph w I2C Backpack: What's better than a single LED? Lots of LEDs! A fun way to make a small linear display is to use two 12-bar Bi-color bar-graphs. Much like our 8x8 and 7-segment backpacks, this backpack pairs perfectly with our bar-graphs and manages all the LED control and multiplexing.
