# Fritzing sketch SprocketFactory (saved by Fritzing 0.9.4b)

parts:
  Part1 = Adafruit Feather M0 Express [part_number="Adafruit #3403"]
  Part2 = Adafruit PWM Servo Featherwing [part_number="Adafruit #2928"]
  Part3 = PowerBoost 500 Charger
  BUTTON1 = Arcade Button (red) [part_number=stop]
  BUTTON2 = Arcade Button (green) [part_number=start]
  Part4 = Lithium Ion Polymer Battery 3.7v 2500mAh [part_number=328]

nets:
  GND: Part1.GND, Part2.GND, Part2.G, Part3.GND, BUTTON1.no_name_yet#2, BUTTON2.no_name_yet#2, Part4.negative
  N1: Part1.TX, Part2.TX
  N2: Part1.RX, Part2.RX
  N3: Part1.MISO, Part2.MISO
  N4: Part1.MOSI, Part2.MOSI
  N5: Part1.SCK, Part2.SCK
  N6: Part1.A5, Part2.F
  N7: Part1.A4, Part2.E
  N8: Part1.A3, Part2.D
  N9: Part1.A2, Part2.C
  N10: Part1.A1, Part2.B
  N11: Part1.A0, Part2.A
  N12: Part1.AREF, Part2.AREF
  +3V3: Part1.+3V3, Part2.+3.3V
  N13: Part1.!RESET, Part2.RESET
  N14: Part1.VBAT, Part2.VBAT, Part3.VBAT, Part4.positive
  N15: Part1.EN, Part2.EN
  N16: Part1.VBUS, Part2.USB
  N17: Part1.D13, Part2.N
  N18: Part1.D12, Part2.M
  N19: Part1.D11, Part2.L
  N20: Part1.D10, Part2.K
  N21: Part1.D9, Part2.J
  N22: Part1.D6, Part2.I, BUTTON2.no_name_yet#1
  N23: Part1.D5, Part2.H, BUTTON1.no_name_yet#1
  N24: Part1.SCL, Part2.SCL
  N25: Part1.SDA, Part2.SDA
  N26: Part2.PWRIN, Part3.5.0V

custom parts:
  Adafruit Feather M0 Express: We love all our Feathers equally, but this Feather is very special. It's our first Feather that is specifically designed for use with CircuitPython! CircuitPython is our beginner-oriented flavor of MicroPython - and as the name hints at, its a small but full-featured version of the popular Python programming language specifically for use with circuitry and electronics. That doesn't mean you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
  Adafruit PWM Servo Featherwing: This is the 8-Channel PWM or Servo​ FeatherWing, you can add 8 x 12-bit PWM outputs to your Feather board. You want to make a cool robot, maybe a hexapod walker, or maybe just a piece of art with a lot of moving parts. Or maybe you want to drive a lot of LEDs with precise PWM output. What now? You could give up OR you could just get our handy PWM and Servo FeatherWing. It's a lot like our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
  PowerBoost 500 Charger: The PowerBoost 500C is a little DC/DC boost converter module that can be powered by any 3.7V LiIon/LiPoly battery, and convert the battery output to 5.2V DC for running your 5V projects. At its heart is a TPS61090 boost converter from TI. This boost converter chip has some really nice extras such as low battery detection, 2A internal switch, synchronous conversion, excellent efficiency, and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
  Arcade Button (red): Adafruit Arcade Button (red)
  Arcade Button (green): Adafruit Arcade Button (green)
  Lithium Ion Polymer Battery 3.7v 2500mAh: Lithium ion polymer (also known as 'lipo' or 'lipoly') batteries are thin, light and powerful. The output ranges from 4.2V when completely charged to 3.7V. This battery has a capacity of 2500mAh for a total of about 10 Wh. The batteries come pre-attached with a genuine 2-pin JST-PH connector as shown and include the necessary protection circuitry.
