# Fritzing sketch WelcomeToGothemCity (saved by Fritzing 0.9.3b)
breadboards: 1

parts:
  Part1 = Adafruit Metro Mini [part_number="Adafruit #2590"]
  Q1 = TIP120 Hi-Current Darlington Transistor
  R1 = Resistor [tolerance=±5% resistance=1k package=THT]
  J1 = Screw terminal - 2 pins [package=THT]
  Part3 = Lithium Ion Polymer Battery 3.7v 500mAh [part_number=1578]
  Part4 = PowerBoost 500 Charger
  R2 = Resistor [tolerance=±5% resistance=2.7 power=3W package=THT]
  HC-SR04_Sensor_1 = HC-SR04 Ultrasonic Distance Sensor

nets:
  N1: Part1.IO8, HC-SR04_Sensor_1.TRIG
  N2: Part1.IO7, HC-SR04_Sensor_1.ECHO
  N3: Part1.IO5, R1.Pin_0
  5V: Part1.+5V, HC-SR04_Sensor_1.VCC
  GND: Part1.GND, Q1.EMITTER, Part3.negative, Part4.GND, HC-SR04_Sensor_1.GND
  N4: Part1.VIN, Part4.5.0V
  N5: Q1.BASE, R1.Pin_1
  N6: Q1.COLLECTOR, R2.Pin_1
  N7: J1.pin1, R2.Pin_0
  VBatt: J1.pin2, Part3.positive, Part4.VBAT

custom parts:
  Adafruit Metro Mini: We sure love the ATmega328 here at Adafruit, and we use them a lot for our own projects. The processor has plenty of GPIO, Analog inputs, hardware UART SPI and I2C, timers and PWM galore - just enough for most simple projects. When we need to go small, we use a Pro Trinket 3V or 5V, but if you want to have USB-to-Serial built in, we reach for an Adafruit METRO Mini. METRO Mini is the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
  Lithium Ion Polymer Battery 3.7v 500mAh: Lithium ion polymer (also known as 'lipo' or 'lipoly') batteries are thin, light and powerful. The output ranges from 4.2V when completely charged to 3.7V. This battery has a capacity of 500mAh for a total of about 1.9 Wh. The batteries come pre-attached with a genuine 2-pin JST-PH connector as shown and include the necessary protection circuitry.
  PowerBoost 500 Charger: The PowerBoost 500C is a little DC/DC boost converter module that can be powered by any 3.7V LiIon/LiPoly battery, and convert the battery output to 5.2V DC for running your 5V projects. At its heart is a TPS61090 boost converter from TI. This boost converter chip has some really nice extras such as low battery detection, 2A internal switch, synchronous conversion, excellent efficiency, and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
