# Fritzing sketch WhyDidTheChicken (saved by Fritzing 0.9.5d)
breadboards: 1

parts:
  Part1 = Adafruit Metro Mini [part_number="Adafruit #2590"]
  Part2 = PowerBoost 500 Charger
  Part3 = Bicolor 8x8 LED Matrix Backpack [part_number=902]
  LED2 = LED - 5mm [color="Yellow (592nm)" package="5 mm [THT]"]
  LED3 = LED - 5mm [color="Green (555nm)" package="5 mm [THT]"]
  R1 = Resistor [tolerance=±5% resistance=150 package=THT]
  J1 = female pin header, 4 pins [form="♀ (female)"]
  J2 = male pin header, 4 pins [form="♂ (male)"]
  R2 = Resistor [tolerance=±5% resistance=150 package=THT]
  R3 = Resistor [tolerance=±5% resistance=150 package=THT]
  J3 = female pin header, 6 pins [form="♀ (female)"]
  J4 = male pin header, 6 pins [form="♂ (male)"]
  S1 = Pushbutton [package="[THT]"]
  LED4 = LED - 5mm [color="Red (635nm)" package="5 mm [THT]"]
  Part4 = Lithium Ion Polymer Battery 3.7v 500mAh [part_number=1578]

nets:
  N1: Part1.AD5/SCL, J1.pin4
  N2: Part1.AD4/SDA, J1.pin3
  N3: Part1.IO12, R1.Pin_0
  N4: Part1.IO11, R2.Pin_0
  N5: Part1.IO10, R3.Pin_0
  N6: Part1.IO9, J3.pin5
  5V: Part1.+5V, J1.pin1, J3.pin1
  GND: Part1.GND, Part2.GND, J1.pin2, J3.pin6
  N7: Part1.VIN, Part2.5.0V
  N8: Part2.GND_BAT_IN, Part4.negative
  N9: Part2.VBAT_IN, Part4.positive
  N10: Part3.SCL, J2.pin4
  N11: Part3.SDA, J2.pin3
  N12: Part3.GND, J2.pin2
  N13: Part3.VDD, J2.pin1
  N14: LED2.cathode, J4.pin3
  N15: LED2.anode, LED3.anode, J4.pin1, LED4.anode
  N16: LED3.cathode, J4.pin4
  N17: R1.Pin_1, J3.pin2
  N18: R2.Pin_1, J3.pin3
  N19: R3.Pin_1, J3.pin4
  N20: J4.pin2, LED4.cathode
  N21: J4.pin5, S1.Pin_3, S1.Pin_4
  N22: J4.pin6, S1.Pin_2

custom parts:
  Adafruit Metro Mini: We sure love the ATmega328 here at Adafruit, and we use them a lot for our own projects. The processor has plenty of GPIO, Analog inputs, hardware UART SPI and I2C, timers and PWM galore - just enough for most simple projects. When we need to go small, we use a Pro Trinket 3V or 5V, but if you want to have USB-to-Serial built in, we reach for an Adafruit METRO Mini. METRO Mini is the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
  Bicolor 8x8 LED Matrix Backpack: This 1.2" bi-color 8x8 LED matrix includes a driver chip for simple control via an I2C interface. It's called a Bicolor LED, but you can have 3 colors total by turning on the red and green LEDs, which creates yellow. That's 3 colors for the price of 2! The backpacks come with address-selection jumpers so you can connect up to eight bicolor matrices on a single I2C bus.
  Lithium Ion Polymer Battery 3.7v 500mAh: Lithium ion polymer (also known as 'lipo' or 'lipoly') batteries are thin, light and powerful. The output ranges from 4.2V when completely charged to 3.7V. This battery has a capacity of 500mAh for a total of about 1.9 Wh. The batteries come pre-attached with a genuine 2-pin JST-PH connector as shown and include the necessary protection circuitry.
